# Fritzing sketch infrared (saved by Fritzing 0.9.10b)
breadboards: 1

parts:
  Bauteil1 = Arduino Nano 33 IOT
  R1 = Resistor [tolerance=±5% power=0.25 resistance=220 package=THT]
  R2 = Resistor [tolerance=±5% power=0.25 resistance=220 package=THT]
  R3 = Resistor [tolerance=±5% power=0.25 resistance=220 package=THT]
  LED2 = RGB LED (com. cathode, rgb) [package="5 mm [THT]"]

nets:
  N1: Bauteil1.RESET, Bauteil1.A7
  N2: Bauteil1.GND, Bauteil1.D13~, LED2.common_cathode
  N3: Bauteil1.D2, R3.Pin_1
  N4: Bauteil1.D3~, R2.Pin_1
  N5: Bauteil1.D5~, R1.Pin_1
  N6: Bauteil1.D11/MOSI, Bauteil1.+5V
  N7: R1.Pin_0, LED2.red_anode
  N8: R2.Pin_0, LED2.green_anode
  N9: R3.Pin_0, LED2.blue_anode

custom parts:
  Arduino Nano 33 IOT: The Arduino Nano 33 IoT is the easiest and cheapest point of entry to enhance existing devices (and creating new ones) to be part of the IoT and designing pico-network applications. Whether you are looking at building a sensor network connected to your office or home router, or if you want to create a BLE device sending data to a cellphone, the Nano 33 IoT is your one-stop-solution for many of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
  RGB LED (com. cathode, rgb): A 5mm tri-color LED with red, green and blue inside.
